// Logisim project przyklad_async.circ as structural Verilog: 4 circuits, main circuit main
module main (
  input  x1,
  input  x0,
  output y
);

  wire and_1_out, and_2_out, and_3_out, and_4_out, and_5_out, and_6_out, and_7_out, and_8_out, and_9_out,
       and_10_out, clock_1_out, d_ff_1_q, d_ff_2_q, d_ff_3_q, not_1_out, not_2_out, not_3_out, not_4_out,
       not_5_out, Q0_out, Q1_out, Q2_out;

  not not_1 (not_1_out, x1);
  not not_2 (not_2_out, x0);
  not not_3 (not_3_out, d_ff_2_q);
  not not_4 (not_4_out, d_ff_1_q);
  not not_5 (not_5_out, d_ff_3_q);
  and and_1 (and_1_out, d_ff_1_q, not_3_out, not_5_out);
  and and_2 (and_2_out, not_1_out, d_ff_1_q, d_ff_2_q);
  and and_3 (and_3_out, x1, not_2_out, d_ff_1_q, d_ff_2_q);
  and and_4 (and_4_out, x0, not_4_out, not_3_out);
  and and_5 (and_5_out, not_1_out, not_2_out, d_ff_1_q, not_5_out);
  and and_6 (and_6_out, x1, x0, d_ff_2_q, not_5_out);
  and and_7 (and_7_out, x1, d_ff_1_q, d_ff_2_q);
  and and_8 (and_8_out, x1, d_ff_1_q, d_ff_3_q);
  and and_9 (and_9_out, not_2_out, d_ff_1_q, not_3_out, d_ff_3_q);
  and and_10 (and_10_out, not_1_out, not_2_out, not_4_out);
  or Q2 (Q2_out, and_1_out, and_2_out, and_3_out, and_4_out, d_ff_3_q);
  or Q1 (Q1_out, and_5_out, and_6_out, and_7_out, and_8_out);
  or Q0 (Q0_out, and_9_out, and_10_out);
  Clock clock_1 (.out(clock_1_out));
  D_Flip_Flop d_ff_1 (.clk(clock_1_out), .D(Q2_out), .Q(d_ff_1_q));  // open: Qn, preset, en, reset
  D_Flip_Flop d_ff_2 (.clk(clock_1_out), .D(Q1_out), .Q(d_ff_2_q));  // open: Qn, preset, en, reset
  D_Flip_Flop d_ff_3 (.clk(clock_1_out), .D(Q0_out), .Q(d_ff_3_q));  // open: Qn, preset, en, reset
  LED Q0_2 (.in(d_ff_3_q));
  LED Q1_2 (.in(d_ff_2_q));
  LED Q2_2 (.in(d_ff_1_q));
  and and_11 (y, d_ff_1_q, d_ff_3_q);
endmodule

// Q2'
module Q2 (
  input  Q2,
  input  Q1,
  input  Q0,
  input  x,
  input  x0,
  output Q2_prime
);

  wire nand_1_out, nand_2_out, nand_3_out, not_1_out, not_2_out, not_3_out, not_4_out;

  not not_1 (not_1_out, Q2);
  not not_2 (not_2_out, Q0);
  not not_3 (not_3_out, x);
  not not_4 (not_4_out, x0);
  nand nand_1 (nand_1_out, not_3_out, not_1_out, Q0);
  nand nand_2 (nand_2_out, not_1_out, Q1);
  nand nand_3 (nand_3_out, Q1, not_2_out);
  nand nand_4 (Q2_prime, nand_1_out, nand_2_out, nand_3_out, not_4_out);
endmodule

// Q1'
module Q1 (
  input  Q2,
  input  Q1,
  input  Q0,
  input  x,
  input  x0,
  output Q1_prime
);

  wire nand_1_out, nand_2_out, nand_3_out, not_1_out, not_2_out, not_3_out, not_4_out, not_5_out;

  not not_1 (not_1_out, Q2);
  not not_2 (not_2_out, Q1);
  not not_3 (not_3_out, Q0);
  not not_4 (not_4_out, x);
  not not_5 (not_5_out, x0);
  nand nand_1 (nand_1_out, not_1_out, Q0);
  nand nand_2 (nand_2_out, not_4_out, Q2, not_3_out);
  nand nand_3 (nand_3_out, not_1_out, not_2_out);
  nand nand_4 (Q1_prime, nand_1_out, nand_2_out, nand_3_out, not_5_out);
endmodule

// Q0'
module Q0 (
  input  Q2,
  input  Q1,
  input  Q0,
  input  x,
  input  x0,
  output Q0_prime
);

  wire nand_1_out, nand_2_out, nand_3_out, nand_4_out, not_1_out, not_2_out, not_3_out, not_4_out;

  not not_1 (not_1_out, Q2);
  not not_2 (not_2_out, Q0);
  not not_3 (not_3_out, x);
  not not_4 (not_4_out, x0);
  nand nand_1 (nand_1_out, not_3_out, not_2_out);
  nand nand_2 (nand_2_out, not_1_out, Q1);
  nand nand_3 (nand_3_out, x, Q0);
  nand nand_4 (nand_4_out, Q1, not_2_out);
  nand nand_5 (Q0_prime, nand_1_out, nand_2_out, nand_3_out, nand_4_out, not_4_out);
endmodule
