// Logisim project przyklad_automat_lab3_JK2.circ as structural Verilog: 4 circuits, main circuit main
module main (
  input  x,
  output y
);

  wire and_1_out, and_2_out, and_3_out, and_4_out, and_5_out, clock_1_out, not_1_out, or_1_out, or_2_out,
       Q0_q, Q0_qn, Q1_q, Q1_qn, Q2_q, Q2_qn;

  not not_1 (not_1_out, x);
  and and_1 (and_1_out, Q2_q, Q1_q);
  and and_2 (and_2_out, Q2_qn, Q1_q, Q0_q, x);
  and and_3 (and_3_out, Q2_qn, Q1_q);
  and and_4 (and_4_out, Q2_qn, Q1_q, not_1_out);
  and and_5 (and_5_out, Q2_qn, Q0_q);
  or or_1 (or_1_out, and_1_out, and_2_out);
  or or_2 (or_2_out, and_3_out, x);
  Clock clock_1 (.out(clock_1_out));
  J_K_Flip_Flop Q2 (.J(and_4_out), .clk(clock_1_out), .K(1'b1), .Q(Q2_q), .Qn(Q2_qn));  // open: preset, en, reset
  J_K_Flip_Flop Q1 (.J(and_5_out), .clk(clock_1_out), .K(or_1_out), .Q(Q1_q), .Qn(Q1_qn));  // open: preset, en, reset
  J_K_Flip_Flop Q0 (.J(or_2_out), .clk(clock_1_out), .K(not_1_out), .Q(Q0_q), .Qn(Q0_qn));  // open: preset, en, reset
  nand nand_1 (y, Q2_q, Q1_q);
endmodule

// Q2'
module Q2 (
  input  Q2,
  input  Q1,
  input  Q0,
  input  x,
  input  x0,
  output Q2_prime_J,
  output Q2_prime_K
);
endmodule

// Q1'
module Q1 (
  input  Q2,
  input  Q1,
  input  Q0,
  input  x,
  input  x0,
  output Q1_prime
);

  wire nand_1_out, nand_2_out, nand_3_out, not_1_out, not_2_out, not_3_out, not_4_out, not_5_out;

  not not_1 (not_1_out, Q2);
  not not_2 (not_2_out, Q0);
  not not_3 (not_3_out, Q1);
  not not_4 (not_4_out, x);
  not not_5 (not_5_out, x0);
  nand nand_1 (nand_1_out, not_1_out, Q0);
  nand nand_2 (nand_2_out, not_4_out, Q2, not_2_out);
  nand nand_3 (nand_3_out, not_1_out, not_3_out);
  nand nand_4 (Q1_prime, nand_1_out, nand_2_out, nand_3_out, not_5_out);
endmodule

// Q0'
module Q0 (
  input  Q2,
  input  Q1,
  input  Q0,
  input  x,
  input  x0,
  output Q0_prime
);

  wire nand_1_out, nand_2_out, nand_3_out, nand_4_out, not_1_out, not_2_out, not_3_out, not_4_out;

  not not_1 (not_1_out, Q2);
  not not_2 (not_2_out, Q0);
  not not_3 (not_3_out, x);
  not not_4 (not_4_out, x0);
  nand nand_1 (nand_1_out, not_3_out, not_2_out);
  nand nand_2 (nand_2_out, not_1_out, Q1);
  nand nand_3 (nand_3_out, x, Q0);
  nand nand_4 (nand_4_out, Q1, not_2_out);
  nand nand_5 (Q0_prime, nand_1_out, nand_2_out, nand_3_out, nand_4_out, not_4_out);
endmodule
