// Logisim project przyklad_mikroprogramowanie.circ as structural Verilog: 1 circuit, main circuit main
module main (
  input  [3:0] A,
  input  [3:0] B
);

  wire _0_q, _1_5_q, _1_q, _2_q, _3_q, _4_q, _5_q, _6_q, and_1_out, and_2_out, and_3_out, and_4_out, Az_q,
       Bz_q, clock_1_out, comparator_1_eq, comparator_2_gt, multiplexer_3_out, not_1_out, not_2_out,
       not_3_out, or_1_out, or_2_out, or_3_out, shift_register_1_out;
  wire [2:0] adder_1_out, Am_q, Bm_q, multiplexer_1_out, multiplexer_2_out, multiplexer_4_out,
       subtractor_1_out;

  Clock clock_1 (.out(clock_1_out));
  or or_1 (or_1_out, _5_q, _4_q, _3_q);
  Multiplexer #(.width(3), .enable("false")) multiplexer_1 (
    .in0(Bm_q), .in1(Am_q), .out(multiplexer_1_out), .sel(_5_q));
  Register #(.width(1)) Az (.D(A[3]), .en(_1_q), .Q(Az_q), .clk(clock_1_out), .clr(_0_q));
  Multiplexer #(.width(3), .enable("false")) multiplexer_2 (
    .in0(Am_q), .in1(Bm_q), .out(multiplexer_2_out), .sel(_5_q));
  Subtractor #(.width(3)) subtractor_1 (
    .a(multiplexer_1_out), .b(multiplexer_2_out), .out(subtractor_1_out));  // open: bin, bout
  not not_1 (not_1_out, _4_q);
  Multiplexer #(.enable("false")) multiplexer_3 (.in0(Bz_q), .in1(Az_q), .out(multiplexer_3_out), .sel(not_1_out));
  Register #(.width(3)) Am (.D(A[2:0]), .en(_1_q), .Q(Am_q), .clk(clock_1_out), .clr(_0_q));
  Multiplexer #(.width(3), .enable("false")) multiplexer_4 (
    .in0(subtractor_1_out), .in1(adder_1_out), .out(multiplexer_4_out), .sel(_3_q));
  Register #(.width(1)) Wz (.D(multiplexer_3_out), .en(or_1_out), .clk(clock_1_out), .clr(_1_q));  // open: Q
  Register #(.width(1)) Bz (.D(B[3]), .en(_1_q), .Q(Bz_q), .clk(clock_1_out), .clr(_0_q));
  Register #(.width(3)) Wm (.D(multiplexer_4_out), .en(or_1_out), .clk(clock_1_out), .clr(_1_q));  // open: Q
  Shift_Register shift_register_1 (
    .clk(clock_1_out), .out(shift_register_1_out));  // open: shift, in, load, clr, d0, q0, d1, q1, d2, q2, d3, q3, d4, q4, d5, q5, d6, q6, d7, q7
  Register #(.width(3)) Bm (.D(B[2:0]), .en(_1_q), .Q(Bm_q), .clk(clock_1_out), .clr(_0_q));
  Comparator #(.width(1), .mode("unsigned")) comparator_1 (.a(Az_q), .b(Bz_q), .eq(comparator_1_eq));  // open: gt, lt
  Comparator #(.width(3), .mode("unsigned")) comparator_2 (.a(Am_q), .b(Bm_q), .gt(comparator_2_gt));  // open: eq, lt
  Adder #(.width(3)) adder_1 (.a(Bm_q), .b(Am_q), .out(adder_1_out));  // open: cin, cout
  D_Flip_Flop _1 (.clk(clock_1_out), .D(_0_q), .Q(_1_q));  // open: Qn, preset, en, reset
  D_Flip_Flop _0 (.clk(clock_1_out), .D(shift_register_1_out), .Q(_0_q));  // open: Qn, preset, en, reset
  D_Flip_Flop _1_5 (.clk(clock_1_out), .D(_1_q), .Q(_1_5_q));  // open: Qn, preset, en, reset
  not not_2 (not_2_out, comparator_1_eq);
  and and_1 (and_1_out, comparator_1_eq, _1_5_q);
  and and_2 (and_2_out, not_2_out, _1_5_q);
  D_Flip_Flop _3 (.clk(clock_1_out), .D(and_1_out), .Q(_3_q));  // open: Qn, preset, en, reset
  D_Flip_Flop _2 (.clk(clock_1_out), .D(and_2_out), .Q(_2_q));  // open: Qn, preset, en, reset
  and and_3 (and_3_out, comparator_2_gt, _2_q);
  not not_3 (not_3_out, comparator_2_gt);
  and and_4 (and_4_out, not_3_out, _2_q);
  D_Flip_Flop _5 (.clk(clock_1_out), .D(and_3_out), .Q(_5_q));  // open: Qn, preset, en, reset
  D_Flip_Flop _4 (.clk(clock_1_out), .D(and_4_out), .Q(_4_q));  // open: Qn, preset, en, reset
  or or_2 (or_2_out, _5_q, _4_q, _3_q);
  D_Flip_Flop _6 (.clk(clock_1_out), .D(or_3_out), .Q(_6_q));  // open: Qn, preset, en, reset
  or or_3 (or_3_out, _6_q, or_2_out);

  // Notes on the sheet:
  //   S1
  //   S3
  //   S2
  //   S4
  //   S0
endmodule
